// Logisim project Conditional_Adder.circ as structural Verilog: 1 circuit, main circuit Cond_Add
module Cond_Add (
  input  P0,
  input  P1,
  input  P2,
  input  P3,
  output out0,
  output out1,
  output out2,
  output out3
);

  wire adder_1_cout;
  wire [3:0] adder_2_out;

  Adder #(.width(4)) adder_1 (.a({P3, P2, P1, P0}), .b(4'b1010), .cin(1'b1), .cout(adder_1_cout));  // open: out
  Adder #(.width(4)) adder_2 (.a({P3, P2, P1, P0}), .b(4'b0011), .out(adder_2_out));  // open: cin, cout
  Multiplexer #(.width(4)) multiplexer_1 (
    .in0({P3, P2, P1, P0}), .in1(adder_2_out), .out({out3, out2, out1, out0}), .sel(adder_1_cout));
endmodule
