// Logisim project Double_Dabble_circuit.circ as structural Verilog: 1 circuit, main circuit Double_Dabble
module Double_Dabble (
  input  [3:0] D3,
  input  [3:0] D2,
  input  [3:0] D1,
  input  in_4,
  input  [3:0] D0,
  input  in_6,
  input  LDD,
  input  rst,
  output [3:0] out_9,
  output [3:0] out_10,
  output [3:0] out_11,
  output [3:0] out_12,
  output [3:0] out_13,
  output [3:0] out_14
);

  wire adder_1_cout, adder_3_cout, adder_5_cout, adder_7_cout, and_1_out, clock_1_out, nand_1_out, not_1_out,
       not_2_out, not_3_out, not_4_out, not_5_out, or_1_out, shift_left_reg_2_q3, shift_left_reg_3_q3,
       t_ff_1_q, t_ff_2_q, t_ff_3_q, t_ff_4_q, xor_1_out, xor_2_out, xor_3_out, xor_4_out;
  wire [3:0] adder_2_out, adder_4_out, adder_6_out, adder_8_out, counter_1_q;

  Clock clock_1 (.out(clock_1_out));
  T_Flip_Flop t_ff_1 (.T(adder_1_cout), .clk(clock_1_out), .Q(t_ff_1_q));  // open: Qn, reset, preset
  shift_left_reset shift_left_reset_1 (
    .D3(adder_2_out[3]), .D2(adder_2_out[2]), .D1(adder_2_out[1]), .D0(adder_2_out[0]), .SIN(out_12[3]),
    .LOAD(xor_1_out), .ENABLE(not_5_out), .rst(rst), .CLK(clock_1_out), .q3(out_11[3]), .q2(out_11[2]),
    .q1(out_11[1]), .q0(out_11[0]));
  Adder #(.width(4)) adder_1 (.a(out_11), .b(4'b1010), .cin(1'b1), .cout(adder_1_cout));  // open: out
  xor xor_1 (xor_1_out, adder_1_cout, t_ff_1_q);
  shift_left_reg shift_left_reg_1 (
    .D3(D3[3]), .D2(D3[2]), .D1(D3[1]), .D0(D3[0]), .SIN(shift_left_reg_2_q3), .LOAD(LDD),
    .ENABLE(and_1_out), .CLK(clock_1_out), .q3(out_9[3]), .q2(out_9[2]), .q1(out_9[1]), .q0(out_9[0]));
  Adder #(.width(4)) adder_2 (.a(out_11), .b(4'b0011), .out(adder_2_out), .cin(1'b0));  // open: cout
  T_Flip_Flop t_ff_2 (.T(adder_3_cout), .clk(clock_1_out), .Q(t_ff_2_q));  // open: Qn, reset, preset
  not not_1 (not_1_out, xor_1_out);
  not not_2 (not_2_out, xor_2_out);
  xor xor_2 (xor_2_out, adder_3_cout, t_ff_2_q);
  shift_left_reg shift_left_reg_2 (
    .D3(D2[3]), .D2(D2[2]), .D1(D2[1]), .D0(D2[0]), .SIN(shift_left_reg_3_q3), .LOAD(LDD),
    .ENABLE(nand_1_out), .CLK(clock_1_out), .q3(shift_left_reg_2_q3));  // open: q2, q1, q0
  shift_left_reset shift_left_reset_2 (
    .D3(adder_4_out[3]), .D2(adder_4_out[2]), .D1(adder_4_out[1]), .D0(adder_4_out[0]), .SIN(out_13[3]),
    .LOAD(xor_2_out), .ENABLE(not_5_out), .rst(rst), .CLK(clock_1_out), .q3(out_12[3]), .q2(out_12[2]),
    .q1(out_12[1]), .q0(out_12[0]));
  Adder #(.width(4)) adder_3 (.a(out_12), .b(4'b1010), .cin(1'b1), .cout(adder_3_cout));  // open: out
  and and_1 (and_1_out, not_1_out, not_2_out, not_3_out, not_4_out);
  not not_3 (not_3_out, xor_3_out);
  Adder #(.width(4)) adder_4 (.a(out_12), .b(4'b0011), .out(adder_4_out), .cin(1'b0));  // open: cout
  not not_4 (not_4_out, xor_4_out);
  shift_left_reg shift_left_reg_3 (
    .D3(D1[3]), .D2(D1[2]), .D1(D1[1]), .D0(D1[0]), .SIN(out_10[3]), .LOAD(LDD), .ENABLE(nand_1_out),
    .CLK(clock_1_out), .q3(shift_left_reg_3_q3));  // open: q2, q1, q0
  not not_5 (not_5_out, or_1_out);
  or or_1 (or_1_out, xor_1_out, xor_2_out, xor_3_out, xor_4_out);
  shift_left_reset shift_left_reset_3 (
    .D3(adder_6_out[3]), .D2(adder_6_out[2]), .D1(adder_6_out[1]), .D0(adder_6_out[0]), .SIN(out_14[3]),
    .LOAD(xor_3_out), .ENABLE(not_5_out), .rst(rst), .CLK(clock_1_out), .q3(out_13[3]), .q2(out_13[2]),
    .q1(out_13[1]), .q0(out_13[0]));
  T_Flip_Flop t_ff_3 (.T(adder_5_cout), .clk(clock_1_out), .Q(t_ff_3_q));  // open: Qn, reset, preset
  xor xor_3 (xor_3_out, adder_5_cout, t_ff_3_q);
  Adder #(.width(4)) adder_5 (.a(out_13), .b(4'b1010), .cin(1'b1), .cout(adder_5_cout));  // open: out
  shift_left_reg shift_left_reg_4 (
    .D3(D0[3]), .D2(D0[2]), .D1(D0[1]), .D0(D0[0]), .SIN(1'b0), .LOAD(LDD), .ENABLE(nand_1_out),
    .CLK(clock_1_out), .q3(out_10[3]), .q2(out_10[2]), .q1(out_10[1]), .q0(out_10[0]));
  Adder #(.width(4)) adder_6 (.a(out_13), .b(4'b0011), .out(adder_6_out), .cin(1'b0));  // open: cout
  shift_left_reset shift_left_reset_4 (
    .D3(adder_8_out[3]), .D2(adder_8_out[2]), .D1(adder_8_out[1]), .D0(adder_8_out[0]), .SIN(out_9[3]),
    .LOAD(xor_4_out), .ENABLE(not_5_out), .rst(rst), .CLK(clock_1_out), .q3(out_14[3]), .q2(out_14[2]),
    .q1(out_14[1]), .q0(out_14[0]));
  Counter #(.max('hf), .width(4)) counter_1 (
    .clr(in_4), .load(in_6), .up(1'b1), .count(nand_1_out), .clk(clock_1_out), .D(D2), .Q(counter_1_q));  // open: carry
  Adder #(.width(4)) adder_7 (.a(out_14), .b(4'b1010), .cin(1'b1), .cout(adder_7_cout));  // open: out
  T_Flip_Flop t_ff_4 (.T(adder_7_cout), .clk(clock_1_out), .Q(t_ff_4_q));  // open: Qn, reset, preset
  nand nand_1 (nand_1_out, counter_1_q[3], counter_1_q[2], counter_1_q[1], counter_1_q[0]);
  Adder #(.width(4)) adder_8 (.a(out_14), .b(4'b0011), .out(adder_8_out), .cin(1'b0));  // open: cout
  xor xor_4 (xor_4_out, adder_7_cout, t_ff_4_q);

  // Notes on the sheet:
  //   product register
  //   second 4 bits
  //   second 4 bits
  //   first 4 bits
  //   first 4 bits
endmodule
