// Logisim project Left_Side.circ as structural Verilog: 1 circuit, main circuit Left_side
module Left_side (
  input  [7:0] A,
  input  LA,
  input  EA,
  input  EP,
  input  b0,
  input  Clk,
  input  rst,
  output [15:0] out_put
);

  wire [7:0] multiplexer_2_out, two_comp_new_1_q0;
  wire [15:0] adder_1_out, multiplexer_1_out, shift_left_reg_1_q0;

  Adder #(.width(16)) adder_1 (.a(shift_left_reg_1_q0), .b(out_put), .out(adder_1_out), .cin(1'b0));  // open: cout
  Multiplexer #(.width(16)) multiplexer_1 (.in0({16{1'b0}}), .in1(adder_1_out), .out(multiplexer_1_out), .sel(b0));
  two_comp_new two_comp_new_1 (
    .b7(A[7]), .b6(A[6]), .b5(A[5]), .b4(A[4]), .b3(A[3]), .b2(A[2]), .b1(A[1]), .b0(A[0]),
    .Q0(two_comp_new_1_q0[0]), .Q1(two_comp_new_1_q0[1]), .Q2(two_comp_new_1_q0[2]),
    .Q3(two_comp_new_1_q0[3]), .Q4(two_comp_new_1_q0[4]), .Q5(two_comp_new_1_q0[5]),
    .Q6(two_comp_new_1_q0[6]), .Q7(two_comp_new_1_q0[7]));
  Register #(.width(16)) register_1 (.D(multiplexer_1_out), .en(EP), .clk(Clk), .Q(out_put), .clr(rst));
  Multiplexer #(.width(8)) multiplexer_2 (.in0(A), .in1(two_comp_new_1_q0), .out(multiplexer_2_out), .sel(A[7]));
  shift_left_reg shift_left_reg_1 (
    .D3(multiplexer_2_out[3]), .D2(multiplexer_2_out[2]), .D1(multiplexer_2_out[1]),
    .D0(multiplexer_2_out[0]), .SIN(1'b0), .LOAD(LA), .ENABLE(EA), .CLK(Clk), .q3(shift_left_reg_1_q0[3]),
    .q2(shift_left_reg_1_q0[2]), .q1(shift_left_reg_1_q0[1]), .q0(shift_left_reg_1_q0[0]));
  shift_left_reg shift_left_reg_2 (
    .D3(multiplexer_2_out[7]), .D2(multiplexer_2_out[6]), .D1(multiplexer_2_out[5]),
    .D0(multiplexer_2_out[4]), .SIN(shift_left_reg_1_q0[3]), .LOAD(LA), .ENABLE(EA), .CLK(Clk),
    .q3(shift_left_reg_1_q0[7]), .q2(shift_left_reg_1_q0[6]), .q1(shift_left_reg_1_q0[5]),
    .q0(shift_left_reg_1_q0[4]));
  shift_left_reg shift_left_reg_3 (
    .D3(1'b0), .D2(1'b0), .D1(1'b0), .D0(1'b0), .SIN(shift_left_reg_1_q0[7]), .LOAD(LA), .ENABLE(EA),
    .CLK(Clk), .q3(shift_left_reg_1_q0[11]), .q2(shift_left_reg_1_q0[10]), .q1(shift_left_reg_1_q0[9]),
    .q0(shift_left_reg_1_q0[8]));
  shift_left_reg shift_left_reg_4 (
    .D3(1'b0), .D2(1'b0), .D1(1'b0), .D0(1'b0), .SIN(shift_left_reg_1_q0[11]), .LOAD(LA), .ENABLE(EA),
    .CLK(Clk), .q3(shift_left_reg_1_q0[15]), .q2(shift_left_reg_1_q0[14]), .q1(shift_left_reg_1_q0[13]),
    .q0(shift_left_reg_1_q0[12]));

  // Notes on the sheet:
  //   first 4 bits
  //   second 4 bits
endmodule
