// Logisim project bcd_shift_reg.circ as structural Verilog: 3 circuits, main circuit bcd_shifter_main
module bcd_shifter_main (
  input  rst,
  input  [3:0] D2,
  input  [3:0] D1,
  input  [3:0] D0,
  input  [3:0] input_right,
  input  [3:0] input_left,
  input  ENABLE,
  input  LOAD,
  input  CLK,
  output [3:0] Q2,
  output [3:0] Q1,
  output [3:0] Q0
);

  wire [3:0] multiplexer_1_out, multiplexer_2_out, multiplexer_3_out;

  Multiplexer #(.select(2), .width(4)) multiplexer_1 (
    .in0(Q2), .in1(input_right), .in2(Q1), .in3(D2), .out(multiplexer_1_out), .sel({LOAD, ENABLE}));
  Register #(.width(4)) register_1 (.D(multiplexer_1_out), .en(1'b1), .clk(CLK), .Q(Q2), .clr(rst));
  Multiplexer #(.select(2), .width(4)) multiplexer_2 (
    .in0(Q1), .in1(Q2), .in2(Q0), .in3(D1), .out(multiplexer_2_out), .sel({LOAD, ENABLE}));
  Register #(.width(4)) register_2 (.D(multiplexer_2_out), .en(1'b1), .clk(CLK), .Q(Q1), .clr(rst));
  Multiplexer #(.select(2), .width(4)) multiplexer_3 (
    .in0(Q0), .in1(Q1), .in2(input_left), .in3(D0), .out(multiplexer_3_out), .sel({LOAD, ENABLE}));
  Register #(.width(4)) register_3 (.D(multiplexer_3_out), .en(1'b1), .clk(CLK), .Q(Q0), .clr(rst));
endmodule

module bcd_all (
  input  flag,
  input  [3:0] D5,
  input  [3:0] D4,
  input  [3:0] D3,
  input  [3:0] D2,
  input  [3:0] D1,
  input  sig_left,
  input  sig_right,
  input  CLK,
  output [3:0] Q1,
  output [3:0] Q2,
  output [3:0] Q3
);

  wire and_2_out, multiplexer_1_out, multiplexer_2_out, multiplexer_3_out, multiplexer_4_out, not_1_out,
       not_2_out, not_3_out, not_4_out, not_5_out, not_6_out, not_7_out, not_8_out, not_9_out;
  wire [1:0] and_3_out;
  wire [3:0] bcd_shifter_side_1_q0, bcd_shifter_side_1_q1, bcd_shifter_side_2_q0, bcd_shifter_side_2_q1,
       nor_1_out;

  not not_1 (not_1_out, bcd_shifter_side_1_q1[2]);
  not not_2 (not_2_out, bcd_shifter_side_1_q1[1]);
  not not_3 (not_3_out, bcd_shifter_side_1_q1[0]);
  not not_4 (not_4_out, bcd_shifter_side_1_q1[3]);
  and and_1 (and_3_out[1], not_4_out, not_1_out, not_2_out, not_3_out);
  bcd_shifter_side bcd_shifter_side_1 (
    .rst(flag), .input_left(Q3), .input_right(4'b0000), .D1(D5), .D0(D4), .ENABLE(multiplexer_3_out),
    .LOAD(multiplexer_4_out), .CLK(CLK), .Q1(bcd_shifter_side_1_q1), .Q0(bcd_shifter_side_1_q0));
  assign nor_1_out = ~(bcd_shifter_side_2_q0 | bcd_shifter_side_2_q1 | bcd_shifter_side_1_q0 | bcd_shifter_side_1_q1 | Q3 | Q1 | Q2);  // NOR_Gate nor_1, 4 bits wide
  Multiplexer #(.select(2)) multiplexer_1 (
    .in0(sig_left), .in1(1'b0), .in2(sig_left), .in3(sig_left), .out(multiplexer_1_out), .sel(and_3_out));
  not not_5 (not_5_out, flag);
  Multiplexer #(.select(2)) multiplexer_2 (
    .in0(sig_right), .in1(sig_right), .in2(1'b0), .in3(sig_right), .out(multiplexer_2_out), .sel(and_3_out));
  and and_2 (and_2_out, nor_1_out[0], nor_1_out[1], nor_1_out[2], nor_1_out[3], not_5_out);
  bcd_shifter_main bcd_shifter_main_1 (
    .rst(flag), .D2(D3), .D1(D2), .D0(D1), .input_right(bcd_shifter_side_1_q0),
    .input_left(bcd_shifter_side_2_q1), .ENABLE(multiplexer_3_out), .LOAD(multiplexer_4_out), .CLK(CLK),
    .Q2(Q3), .Q1(Q2), .Q0(Q1));
  Multiplexer multiplexer_3 (.in0(multiplexer_2_out), .in1(1'b1), .out(multiplexer_3_out), .sel(and_2_out));
  Multiplexer multiplexer_4 (.in0(multiplexer_1_out), .in1(1'b1), .out(multiplexer_4_out), .sel(and_2_out));
  not not_6 (not_6_out, bcd_shifter_side_2_q0[3]);
  not not_7 (not_7_out, bcd_shifter_side_2_q0[2]);
  not not_8 (not_8_out, bcd_shifter_side_2_q0[1]);
  not not_9 (not_9_out, bcd_shifter_side_2_q0[0]);
  and and_3 (and_3_out[0], not_6_out, not_7_out, not_8_out, not_9_out);
  bcd_shifter_side bcd_shifter_side_2 (
    .rst(flag), .input_left(4'b0000), .input_right(Q1), .D1(4'b0000), .D0(4'b0000),
    .ENABLE(multiplexer_3_out), .LOAD(multiplexer_4_out), .CLK(CLK), .Q1(bcd_shifter_side_2_q1),
    .Q0(bcd_shifter_side_2_q0));

  // Notes on the sheet:
  //   LO
  //   EN
endmodule

module bcd_shifter_side (
  input  rst,
  input  [3:0] input_left,
  input  [3:0] input_right,
  input  [3:0] D1,
  input  [3:0] D0,
  input  ENABLE,
  input  LOAD,
  input  CLK,
  output [3:0] Q1,
  output [3:0] Q0
);

  wire [3:0] multiplexer_1_out, multiplexer_2_out;

  Multiplexer #(.select(2), .width(4)) multiplexer_1 (
    .in0(Q1), .in1(input_right), .in2(Q0), .in3(D1), .out(multiplexer_1_out), .sel({LOAD, ENABLE}));
  Register #(.width(4)) register_1 (.D(multiplexer_1_out), .en(1'b1), .clk(CLK), .Q(Q1), .clr(rst));
  Multiplexer #(.select(2), .width(4)) multiplexer_2 (
    .in0(Q0), .in1(Q1), .in2(input_left), .in3(D0), .out(multiplexer_2_out), .sel({LOAD, ENABLE}));
  Register #(.width(4)) register_2 (.D(multiplexer_2_out), .en(1'b1), .clk(CLK), .Q(Q0), .clr(rst));
endmodule
