// Logisim project DD.circ as structural Verilog: 1 circuit, main circuit DD_C
module DD_C (
  input  [14:0] Product,
  output [3:0] Q1,
  output [3:0] Q0,
  output [3:0] Q2,
  output [3:0] Q4,
  output [3:0] Q3
);

  wire cond_add_1_out0, cond_add_1_out1, cond_add_1_out2, cond_add_1_out3, cond_add_2_out0, cond_add_2_out1,
       cond_add_2_out2, cond_add_2_out3, cond_add_3_out0, cond_add_3_out1, cond_add_3_out2, cond_add_3_out3,
       cond_add_4_out0, cond_add_4_out1, cond_add_4_out2, cond_add_6_out0, cond_add_6_out1, cond_add_6_out2,
       cond_add_6_out3, cond_add_7_out0, cond_add_7_out1, cond_add_7_out2, cond_add_7_out3, cond_add_8_out0,
       cond_add_8_out1, cond_add_8_out2, cond_add_8_out3, cond_add_9_out0, cond_add_9_out1, cond_add_9_out2,
       cond_add_9_out3, cond_add_10_out0, cond_add_10_out1, cond_add_10_out2, cond_add_10_out3,
       cond_add_11_out0, cond_add_11_out1, cond_add_11_out2, cond_add_11_out3, cond_add_12_out0,
       cond_add_12_out1, cond_add_12_out2, cond_add_12_out3, cond_add_13_out0, cond_add_13_out1,
       cond_add_13_out2, cond_add_13_out3, cond_add_14_out0, cond_add_14_out1, cond_add_14_out2,
       cond_add_14_out3, cond_add_16_out0, cond_add_16_out1, cond_add_16_out2, cond_add_16_out3,
       cond_add_17_out0, cond_add_17_out1, cond_add_17_out2, cond_add_17_out3, cond_add_18_out0,
       cond_add_18_out1, cond_add_18_out2, cond_add_18_out3, cond_add_19_out0, cond_add_19_out1,
       cond_add_19_out2, cond_add_19_out3, cond_add_20_out0, cond_add_20_out1, cond_add_20_out2,
       cond_add_20_out3, cond_add_21_out0, cond_add_21_out1, cond_add_21_out2, cond_add_21_out3,
       cond_add_22_out0, cond_add_22_out1, cond_add_22_out2, cond_add_22_out3, cond_add_23_out0,
       cond_add_23_out1, cond_add_23_out2, cond_add_23_out3, cond_add_24_out0, cond_add_24_out1,
       cond_add_24_out2, cond_add_24_out3, cond_add_25_out0, cond_add_25_out1, cond_add_25_out2,
       cond_add_25_out3, cond_add_26_out0, cond_add_26_out1, cond_add_26_out2, cond_add_26_out3,
       cond_add_27_out0, cond_add_27_out1, cond_add_27_out2, cond_add_27_out3, cond_add_28_out0,
       cond_add_28_out1, cond_add_28_out2, cond_add_28_out3, cond_add_29_out0, cond_add_29_out1,
       cond_add_29_out2, cond_add_29_out3, cond_add_31_out0, cond_add_31_out1, cond_add_31_out2,
       cond_add_31_out3, cond_add_32_out0, cond_add_32_out1, cond_add_32_out2, cond_add_32_out3,
       cond_add_33_out0, cond_add_33_out1, cond_add_33_out2, cond_add_33_out3, cond_add_34_out0,
       cond_add_34_out1, cond_add_34_out2, cond_add_34_out3, cond_add_35_out0, cond_add_35_out1,
       cond_add_35_out2, cond_add_35_out3, cond_add_36_out0, cond_add_36_out1, cond_add_36_out2,
       cond_add_36_out3, cond_add_37_out0, cond_add_37_out1, cond_add_37_out2, cond_add_37_out3,
       cond_add_38_out0, cond_add_38_out1, cond_add_38_out2, cond_add_38_out3, cond_add_39_out0,
       cond_add_39_out1, cond_add_39_out2, cond_add_39_out3, cond_add_40_out0, cond_add_40_out1,
       cond_add_40_out2, cond_add_40_out3, cond_add_42_out0, cond_add_42_out1, cond_add_42_out2,
       cond_add_42_out3, cond_add_43_out0, cond_add_43_out1, cond_add_43_out2, cond_add_43_out3;

  Cond_Add cond_add_1 (
    .P0(cond_add_9_out3), .P1(cond_add_8_out3), .P2(cond_add_7_out3), .P3(1'b0), .out0(cond_add_1_out0),
    .out1(cond_add_1_out1), .out2(cond_add_1_out2), .out3(cond_add_1_out3));
  Cond_Add cond_add_2 (
    .P0(cond_add_10_out3), .P1(cond_add_1_out0), .P2(cond_add_1_out1), .P3(cond_add_1_out2),
    .out0(cond_add_2_out0), .out1(cond_add_2_out1), .out2(cond_add_2_out2), .out3(cond_add_2_out3));
  Cond_Add cond_add_3 (
    .P0(cond_add_6_out3), .P1(cond_add_2_out3), .P2(cond_add_1_out3), .P3(1'b0), .out0(cond_add_3_out0),
    .out1(cond_add_3_out1), .out2(cond_add_3_out2), .out3(cond_add_3_out3));
  Cond_Add cond_add_4 (
    .P0(cond_add_13_out3), .P1(cond_add_3_out0), .P2(cond_add_3_out1), .P3(cond_add_3_out2),
    .out0(cond_add_4_out0), .out1(cond_add_4_out1), .out2(cond_add_4_out2));  // open: out3
  Cond_Add cond_add_5 (
    .P0(cond_add_14_out3), .P1(cond_add_4_out0), .P2(cond_add_4_out1), .P3(cond_add_4_out2), .out0(Q4[1]),
    .out1(Q4[2]), .out2(Q4[3]));  // open: out3
  Cond_Add cond_add_6 (
    .P0(cond_add_11_out3), .P1(cond_add_2_out0), .P2(cond_add_2_out1), .P3(cond_add_2_out2),
    .out0(cond_add_6_out0), .out1(cond_add_6_out1), .out2(cond_add_6_out2), .out3(cond_add_6_out3));
  Cond_Add cond_add_7 (
    .P0(cond_add_18_out3), .P1(cond_add_17_out3), .P2(cond_add_16_out3), .P3(1'b0), .out0(cond_add_7_out0),
    .out1(cond_add_7_out1), .out2(cond_add_7_out2), .out3(cond_add_7_out3));
  Cond_Add cond_add_8 (
    .P0(cond_add_19_out3), .P1(cond_add_7_out0), .P2(cond_add_7_out1), .P3(cond_add_7_out2),
    .out0(cond_add_8_out0), .out1(cond_add_8_out1), .out2(cond_add_8_out2), .out3(cond_add_8_out3));
  Cond_Add cond_add_9 (
    .P0(cond_add_20_out3), .P1(cond_add_8_out0), .P2(cond_add_8_out1), .P3(cond_add_8_out2),
    .out0(cond_add_9_out0), .out1(cond_add_9_out1), .out2(cond_add_9_out2), .out3(cond_add_9_out3));
  Cond_Add cond_add_10 (
    .P0(cond_add_21_out3), .P1(cond_add_9_out0), .P2(cond_add_9_out1), .P3(cond_add_9_out2),
    .out0(cond_add_10_out0), .out1(cond_add_10_out1), .out2(cond_add_10_out2), .out3(cond_add_10_out3));
  Cond_Add cond_add_11 (
    .P0(cond_add_25_out3), .P1(cond_add_10_out0), .P2(cond_add_10_out1), .P3(cond_add_10_out2),
    .out0(cond_add_11_out0), .out1(cond_add_11_out1), .out2(cond_add_11_out2), .out3(cond_add_11_out3));
  Cond_Add cond_add_12 (
    .P0(cond_add_26_out3), .P1(cond_add_11_out0), .P2(cond_add_11_out1), .P3(cond_add_11_out2),
    .out0(cond_add_12_out0), .out1(cond_add_12_out1), .out2(cond_add_12_out2), .out3(cond_add_12_out3));
  Cond_Add cond_add_13 (
    .P0(cond_add_12_out3), .P1(cond_add_6_out0), .P2(cond_add_6_out1), .P3(cond_add_6_out2),
    .out0(cond_add_13_out0), .out1(cond_add_13_out1), .out2(cond_add_13_out2), .out3(cond_add_13_out3));
  Cond_Add cond_add_14 (
    .P0(cond_add_28_out3), .P1(cond_add_13_out0), .P2(cond_add_13_out1), .P3(cond_add_13_out2),
    .out0(cond_add_14_out0), .out1(cond_add_14_out1), .out2(cond_add_14_out2), .out3(cond_add_14_out3));
  Cond_Add cond_add_15 (
    .P0(cond_add_29_out3), .P1(cond_add_14_out0), .P2(cond_add_14_out1), .P3(cond_add_14_out2), .out0(Q3[1]),
    .out1(Q3[2]), .out2(Q3[3]), .out3(Q4[0]));
  Cond_Add cond_add_16 (
    .P0(cond_add_23_out3), .P1(cond_add_22_out3), .P2(1'b0), .P3(1'b0), .out0(cond_add_16_out0),
    .out1(cond_add_16_out1), .out2(cond_add_16_out2), .out3(cond_add_16_out3));
  Cond_Add cond_add_17 (
    .P0(cond_add_24_out3), .P1(cond_add_16_out0), .P2(cond_add_16_out1), .P3(cond_add_16_out2),
    .out0(cond_add_17_out0), .out1(cond_add_17_out1), .out2(cond_add_17_out2), .out3(cond_add_17_out3));
  Cond_Add cond_add_18 (
    .P0(cond_add_31_out3), .P1(cond_add_17_out0), .P2(cond_add_17_out1), .P3(cond_add_17_out2),
    .out0(cond_add_18_out0), .out1(cond_add_18_out1), .out2(cond_add_18_out2), .out3(cond_add_18_out3));
  Cond_Add cond_add_19 (
    .P0(cond_add_32_out3), .P1(cond_add_18_out0), .P2(cond_add_18_out1), .P3(cond_add_18_out2),
    .out0(cond_add_19_out0), .out1(cond_add_19_out1), .out2(cond_add_19_out2), .out3(cond_add_19_out3));
  Cond_Add cond_add_20 (
    .P0(cond_add_33_out3), .P1(cond_add_19_out0), .P2(cond_add_19_out1), .P3(cond_add_19_out2),
    .out0(cond_add_20_out0), .out1(cond_add_20_out1), .out2(cond_add_20_out2), .out3(cond_add_20_out3));
  Cond_Add cond_add_21 (
    .P0(cond_add_34_out3), .P1(cond_add_20_out0), .P2(cond_add_20_out1), .P3(cond_add_20_out2),
    .out0(cond_add_21_out0), .out1(cond_add_21_out1), .out2(cond_add_21_out2), .out3(cond_add_21_out3));
  Cond_Add cond_add_22 (
    .P0(Product[14]), .P1(1'b0), .P2(1'b0), .P3(1'b0), .out0(cond_add_22_out0), .out1(cond_add_22_out1),
    .out2(cond_add_22_out2), .out3(cond_add_22_out3));
  Cond_Add cond_add_23 (
    .P0(Product[13]), .P1(cond_add_22_out0), .P2(cond_add_22_out1), .P3(cond_add_22_out2),
    .out0(cond_add_23_out0), .out1(cond_add_23_out1), .out2(cond_add_23_out2), .out3(cond_add_23_out3));
  Cond_Add cond_add_24 (
    .P0(Product[12]), .P1(cond_add_23_out0), .P2(cond_add_23_out1), .P3(cond_add_23_out2),
    .out0(cond_add_24_out0), .out1(cond_add_24_out1), .out2(cond_add_24_out2), .out3(cond_add_24_out3));
  Cond_Add cond_add_25 (
    .P0(cond_add_35_out3), .P1(cond_add_21_out0), .P2(cond_add_21_out1), .P3(cond_add_21_out2),
    .out0(cond_add_25_out0), .out1(cond_add_25_out1), .out2(cond_add_25_out2), .out3(cond_add_25_out3));
  Cond_Add cond_add_26 (
    .P0(cond_add_36_out3), .P1(cond_add_25_out0), .P2(cond_add_25_out1), .P3(cond_add_25_out2),
    .out0(cond_add_26_out0), .out1(cond_add_26_out1), .out2(cond_add_26_out2), .out3(cond_add_26_out3));
  Cond_Add cond_add_27 (
    .P0(cond_add_37_out3), .P1(cond_add_26_out0), .P2(cond_add_26_out1), .P3(cond_add_26_out2),
    .out0(cond_add_27_out0), .out1(cond_add_27_out1), .out2(cond_add_27_out2), .out3(cond_add_27_out3));
  Cond_Add cond_add_28 (
    .P0(cond_add_27_out3), .P1(cond_add_12_out0), .P2(cond_add_12_out1), .P3(cond_add_12_out2),
    .out0(cond_add_28_out0), .out1(cond_add_28_out1), .out2(cond_add_28_out2), .out3(cond_add_28_out3));
  Cond_Add cond_add_29 (
    .P0(cond_add_39_out3), .P1(cond_add_28_out0), .P2(cond_add_28_out1), .P3(cond_add_28_out2),
    .out0(cond_add_29_out0), .out1(cond_add_29_out1), .out2(cond_add_29_out2), .out3(cond_add_29_out3));
  Cond_Add cond_add_30 (
    .P0(cond_add_40_out3), .P1(cond_add_29_out0), .P2(cond_add_29_out1), .P3(cond_add_29_out2), .out0(Q2[1]),
    .out1(Q2[2]), .out2(Q2[3]), .out3(Q3[0]));
  Cond_Add cond_add_31 (
    .P0(Product[11]), .P1(cond_add_24_out0), .P2(cond_add_24_out1), .P3(cond_add_24_out2),
    .out0(cond_add_31_out0), .out1(cond_add_31_out1), .out2(cond_add_31_out2), .out3(cond_add_31_out3));
  Cond_Add cond_add_32 (
    .P0(Product[10]), .P1(cond_add_31_out0), .P2(cond_add_31_out1), .P3(cond_add_31_out2),
    .out0(cond_add_32_out0), .out1(cond_add_32_out1), .out2(cond_add_32_out2), .out3(cond_add_32_out3));
  Cond_Add cond_add_33 (
    .P0(Product[9]), .P1(cond_add_32_out0), .P2(cond_add_32_out1), .P3(cond_add_32_out2),
    .out0(cond_add_33_out0), .out1(cond_add_33_out1), .out2(cond_add_33_out2), .out3(cond_add_33_out3));
  Cond_Add cond_add_34 (
    .P0(Product[8]), .P1(cond_add_33_out0), .P2(cond_add_33_out1), .P3(cond_add_33_out2),
    .out0(cond_add_34_out0), .out1(cond_add_34_out1), .out2(cond_add_34_out2), .out3(cond_add_34_out3));
  Cond_Add cond_add_35 (
    .P0(Product[7]), .P1(cond_add_34_out0), .P2(cond_add_34_out1), .P3(cond_add_34_out2),
    .out0(cond_add_35_out0), .out1(cond_add_35_out1), .out2(cond_add_35_out2), .out3(cond_add_35_out3));
  Cond_Add cond_add_36 (
    .P0(Product[6]), .P1(cond_add_35_out0), .P2(cond_add_35_out1), .P3(cond_add_35_out2),
    .out0(cond_add_36_out0), .out1(cond_add_36_out1), .out2(cond_add_36_out2), .out3(cond_add_36_out3));
  Cond_Add cond_add_37 (
    .P0(Product[5]), .P1(cond_add_36_out0), .P2(cond_add_36_out1), .P3(cond_add_36_out2),
    .out0(cond_add_37_out0), .out1(cond_add_37_out1), .out2(cond_add_37_out2), .out3(cond_add_37_out3));
  Cond_Add cond_add_38 (
    .P0(Product[4]), .P1(cond_add_37_out0), .P2(cond_add_37_out1), .P3(cond_add_37_out2),
    .out0(cond_add_38_out0), .out1(cond_add_38_out1), .out2(cond_add_38_out2), .out3(cond_add_38_out3));
  Cond_Add cond_add_39 (
    .P0(cond_add_38_out3), .P1(cond_add_27_out0), .P2(cond_add_27_out1), .P3(cond_add_27_out2),
    .out0(cond_add_39_out0), .out1(cond_add_39_out1), .out2(cond_add_39_out2), .out3(cond_add_39_out3));
  Cond_Add cond_add_40 (
    .P0(cond_add_42_out3), .P1(cond_add_39_out0), .P2(cond_add_39_out1), .P3(cond_add_39_out2),
    .out0(cond_add_40_out0), .out1(cond_add_40_out1), .out2(cond_add_40_out2), .out3(cond_add_40_out3));
  Cond_Add cond_add_41 (
    .P0(cond_add_43_out3), .P1(cond_add_40_out0), .P2(cond_add_40_out1), .P3(cond_add_40_out2), .out0(Q1[1]),
    .out1(Q1[2]), .out2(Q1[3]), .out3(Q2[0]));
  Cond_Add cond_add_42 (
    .P0(Product[3]), .P1(cond_add_38_out0), .P2(cond_add_38_out1), .P3(cond_add_38_out2),
    .out0(cond_add_42_out0), .out1(cond_add_42_out1), .out2(cond_add_42_out2), .out3(cond_add_42_out3));
  Cond_Add cond_add_43 (
    .P0(Product[2]), .P1(cond_add_42_out0), .P2(cond_add_42_out1), .P3(cond_add_42_out2),
    .out0(cond_add_43_out0), .out1(cond_add_43_out1), .out2(cond_add_43_out2), .out3(cond_add_43_out3));
  Cond_Add cond_add_44 (
    .P0(Product[1]), .P1(cond_add_43_out0), .P2(cond_add_43_out1), .P3(cond_add_43_out2), .out0(Q0[1]),
    .out1(Q0[2]), .out2(Q0[3]), .out3(Q1[0]));

  assign Q0[0] = Product[0];
endmodule
