// Logisim project Right_Shift_register.circ as structural Verilog: 1 circuit, main circuit Shift_Right_Register
module Shift_Right_Register (
  input  Enable,
  input  Load,
  input  D8,
  input  D7,
  input  D6,
  input  D5,
  input  D4,
  input  D3,
  input  D2,
  input  D1,
  input  Clock,
  output Q8,
  output Q7,
  output Q6,
  output Q5,
  output Q4,
  output Q3,
  output Q2,
  output Q1
);

  wire multiplexer_1_out, multiplexer_2_out, multiplexer_3_out, multiplexer_4_out, multiplexer_5_out,
       multiplexer_6_out, multiplexer_7_out, multiplexer_8_out;

  Multiplexer #(.select(2)) multiplexer_1 (
    .in0(Q8), .in1(1'b0), .in2(D8), .in3(D8), .out(multiplexer_1_out), .sel({Load, Enable}));
  D_Flip_Flop d_ff_1 (.D(multiplexer_1_out), .clk(Clock), .Q(Q8));  // open: Qn, preset, reset
  Multiplexer #(.select(2)) multiplexer_2 (
    .in0(Q7), .in1(Q8), .in2(D7), .in3(D7), .out(multiplexer_2_out), .sel({Load, Enable}));
  D_Flip_Flop d_ff_2 (.D(multiplexer_2_out), .clk(Clock), .Q(Q7));  // open: Qn, preset, reset
  Multiplexer #(.select(2)) multiplexer_3 (
    .in0(Q6), .in1(Q7), .in2(D6), .in3(D6), .out(multiplexer_3_out), .sel({Load, Enable}));
  D_Flip_Flop d_ff_3 (.D(multiplexer_3_out), .clk(Clock), .Q(Q6));  // open: Qn, preset, reset
  Multiplexer #(.select(2)) multiplexer_4 (
    .in0(Q5), .in1(Q6), .in2(D5), .in3(D5), .out(multiplexer_4_out), .sel({Load, Enable}));
  D_Flip_Flop d_ff_4 (.D(multiplexer_4_out), .clk(Clock), .Q(Q5));  // open: Qn, preset, reset
  Multiplexer #(.select(2)) multiplexer_5 (
    .in0(Q4), .in1(Q5), .in2(D4), .in3(D4), .out(multiplexer_5_out), .sel({Load, Enable}));
  D_Flip_Flop d_ff_5 (.D(multiplexer_5_out), .clk(Clock), .Q(Q4));  // open: Qn, preset, reset
  Multiplexer #(.select(2)) multiplexer_6 (
    .in0(Q3), .in1(Q4), .in2(D3), .in3(D3), .out(multiplexer_6_out), .sel({Load, Enable}));
  D_Flip_Flop d_ff_6 (.D(multiplexer_6_out), .clk(Clock), .Q(Q3));  // open: Qn, preset, reset
  Multiplexer #(.select(2)) multiplexer_7 (
    .in0(Q2), .in1(Q3), .in2(D2), .in3(D2), .out(multiplexer_7_out), .sel({Load, Enable}));
  D_Flip_Flop d_ff_7 (.D(multiplexer_7_out), .clk(Clock), .Q(Q2));  // open: Qn, preset, reset
  Multiplexer #(.select(2)) multiplexer_8 (
    .in0(Q1), .in1(Q2), .in2(D1), .in3(D1), .out(multiplexer_8_out), .sel({Load, Enable}));
  D_Flip_Flop d_ff_8 (.D(multiplexer_8_out), .clk(Clock), .Q(Q1));  // open: Qn, preset, reset

  // Notes on the sheet:
  //   en
  //   load
endmodule
