// Logisim project control_unit_c.circ as structural Verilog: 1 circuit, main circuit control_unit
module control_unit (
  input  Q7A,
  input  rst,
  input  Q7B,
  input  CLK,
  input  B0,
  output LA,
  output LB,
  output SF,
  output flG,
  output psel,
  output EA,
  output EB,
  output EP
);

  wire not_1_out;
  wire [2:0] counter_1_q;

  Counter #(.max('h7), .width(3)) counter_1 (
    .clr(rst), .load(rst), .up(1'b1), .count(EA), .clk(CLK), .D(3'b000), .Q(counter_1_q));  // open: carry
  nand nand_1 (EA, counter_1_q[2], counter_1_q[1], counter_1_q[0]);
  not not_1 (not_1_out, counter_1_q[0]);
  xor xor_1 (SF, Q7A, Q7B);
  and and_1 (flG, not_1_out, counter_1_q[1], counter_1_q[2]);
  or or_1 (EP, B0, rst);

  assign EB = EA;
  assign LA = rst;
  assign LB = rst;
  assign psel = B0;
endmodule
