// Logisim project decoder_seven.circ as structural Verilog: 1 circuit, main circuit seg7_dec
module seg7_dec (
  input  x0,
  input  x1,
  input  x2,
  input  x3,
  output a,
  output b,
  output c,
  output d,
  output e,
  output f,
  output g
);

  wire and_1_out, and_2_out, and_3_out, and_4_out, and_5_out, and_6_out, and_7_out, and_8_out, and_9_out,
       and_10_out, and_11_out, and_12_out, and_13_out, and_14_out, not_1_out, not_2_out, not_3_out,
       not_4_out, not_5_out, not_6_out, not_7_out, not_8_out, or_1_out, or_2_out, or_3_out, or_4_out,
       or_5_out, or_6_out;

  not not_1 (not_1_out, x0);
  not not_2 (not_2_out, x1);
  not not_3 (not_3_out, x2);
  not not_4 (not_4_out, x3);
  and and_1 (and_1_out, x0, not_2_out, not_3_out, not_4_out);
  and and_2 (and_2_out, not_1_out, not_2_out, x2);
  and and_3 (and_3_out, x0, not_2_out, x2);
  and and_4 (and_4_out, not_1_out, x1, x2);
  not not_5 (not_5_out, x0);
  and and_5 (and_5_out, x2, not_2_out, not_5_out);
  and and_6 (and_6_out, x2, x1, x0);
  and and_7 (and_7_out, not_3_out, not_2_out, x0);
  not not_6 (not_6_out, x2);
  not not_7 (not_7_out, x2);
  and and_8 (and_8_out, x1, x0);
  and and_9 (and_9_out, x1, not_6_out);
  and and_10 (and_10_out, not_6_out, x0, not_8_out);
  not not_8 (not_8_out, x3);
  and and_11 (and_11_out, not_2_out, not_7_out, not_8_out);
  and and_12 (and_12_out, x2, not_2_out);
  and and_13 (and_13_out, x0, x1, x2);
  or or_1 (or_1_out, x0, and_12_out);
  or or_2 (or_2_out, and_8_out, and_9_out, and_10_out);
  or or_3 (or_3_out, and_13_out, and_11_out);
  or or_4 (or_4_out, and_1_out, and_2_out);
  or or_5 (or_5_out, and_3_out, and_4_out);
  and and_14 (and_14_out, not_1_out, not_3_out, x1);
  or or_6 (or_6_out, and_7_out, and_5_out, and_6_out);
  not not_9 (a, or_4_out);
  not not_10 (b, or_5_out);
  not not_11 (c, and_14_out);
  not not_12 (d, or_6_out);
  not not_13 (e, or_1_out);
  not not_14 (f, or_2_out);
  not not_15 (g, or_3_out);
endmodule
