// Logisim project shift_left_reset_c.circ as structural Verilog: 1 circuit, main circuit shift_left_reset
module shift_left_reset (
  input  D3,
  input  D2,
  input  D1,
  input  D0,
  input  SIN,
  input  LOAD,
  input  ENABLE,
  input  rst,
  input  CLK,
  output q3,
  output q2,
  output q1,
  output q0
);

  wire multiplexer_1_out, multiplexer_2_out, multiplexer_3_out, multiplexer_4_out;

  Multiplexer #(.select(2)) multiplexer_1 (
    .in0(q3), .in1(q2), .in2(D3), .in3(D3), .out(multiplexer_1_out), .sel({LOAD, ENABLE}));
  D_Flip_Flop d_ff_1 (.D(multiplexer_1_out), .clk(CLK), .Q(q3), .reset(rst));  // open: Qn, preset
  Multiplexer #(.select(2)) multiplexer_2 (
    .in0(q2), .in1(q1), .in2(D2), .in3(D2), .out(multiplexer_2_out), .sel({LOAD, ENABLE}));
  D_Flip_Flop d_ff_2 (.D(multiplexer_2_out), .clk(CLK), .Q(q2), .reset(rst));  // open: Qn, preset
  Multiplexer #(.select(2)) multiplexer_3 (
    .in0(q1), .in1(q0), .in2(D1), .in3(D1), .out(multiplexer_3_out), .sel({LOAD, ENABLE}));
  D_Flip_Flop d_ff_3 (.D(multiplexer_3_out), .clk(CLK), .Q(q1), .reset(rst));  // open: Qn, preset
  Multiplexer #(.select(2)) multiplexer_4 (
    .in0(q0), .in1(SIN), .in2(D0), .in3(D0), .out(multiplexer_4_out), .sel({LOAD, ENABLE}));
  D_Flip_Flop d_ff_4 (.D(multiplexer_4_out), .clk(CLK), .Q(q0), .reset(rst));  // open: Qn, preset
endmodule
