// Logisim project sign_decoder.circ as structural Verilog: 1 circuit, main circuit sign_dec
module sign_dec (
  input  SF,
  output a,
  output b,
  output c,
  output d,
  output e,
  output f,
  output g
);

  Multiplexer multiplexer_1 (.in0(1'b0), .in1(1'b1), .out(g), .sel(SF));

  assign a = 1'b0;
  assign b = 1'b0;
  assign c = 1'b0;
  assign d = 1'b0;
  assign e = 1'b0;
  assign f = 1'b0;
endmodule
