// Logisim project signed_multiplication_right_side.circ as structural Verilog: 1 circuit, main circuit right_side
module right_side (
  input  [7:0] B,
  input  EB,
  input  LB,
  input  clk,
  output z,
  output b0,
  output b7
);

  wire shift_right_register_1_q2, shift_right_register_1_q3, shift_right_register_1_q4,
       shift_right_register_1_q5, shift_right_register_1_q6, shift_right_register_1_q7,
       shift_right_register_1_q8;
  wire [7:0] multiplexer_1_out, two_comp_new_1_q0;

  two_comp_new two_comp_new_1 (
    .b7(B[7]), .b6(B[6]), .b5(B[5]), .b4(B[4]), .b3(B[3]), .b2(B[2]), .b1(B[1]), .b0(B[0]),
    .Q0(two_comp_new_1_q0[0]), .Q1(two_comp_new_1_q0[1]), .Q2(two_comp_new_1_q0[2]),
    .Q3(two_comp_new_1_q0[3]), .Q4(two_comp_new_1_q0[4]), .Q5(two_comp_new_1_q0[5]),
    .Q6(two_comp_new_1_q0[6]), .Q7(two_comp_new_1_q0[7]));
  Multiplexer #(.width(8)) multiplexer_1 (.in0(B), .in1(two_comp_new_1_q0), .out(multiplexer_1_out), .sel(B[7]));
  Shift_Right_Register shift_right_register_1 (
    .Enable(EB), .Load(LB), .D8(multiplexer_1_out[7]), .D7(multiplexer_1_out[6]), .D6(multiplexer_1_out[5]),
    .D5(multiplexer_1_out[4]), .D4(multiplexer_1_out[3]), .D3(multiplexer_1_out[2]),
    .D2(multiplexer_1_out[1]), .D1(multiplexer_1_out[0]), .Clock(clk), .Q8(shift_right_register_1_q8),
    .Q7(shift_right_register_1_q7), .Q6(shift_right_register_1_q6), .Q5(shift_right_register_1_q5),
    .Q4(shift_right_register_1_q4), .Q3(shift_right_register_1_q3), .Q2(shift_right_register_1_q2), .Q1(b0));
  nor nor_1 (z, b0, shift_right_register_1_q2, shift_right_register_1_q3, shift_right_register_1_q4, shift_right_register_1_q5, shift_right_register_1_q6, shift_right_register_1_q7, shift_right_register_1_q8);

  assign b7 = B[7];
endmodule
