// Logisim project two_comp_new_c.circ as structural Verilog: 1 circuit, main circuit two_comp_new
module two_comp_new (
  input  b7,
  input  b6,
  input  b5,
  input  b4,
  input  b3,
  input  b2,
  input  b1,
  input  b0,
  output Q0,
  output Q1,
  output Q2,
  output Q3,
  output Q4,
  output Q5,
  output Q6,
  output Q7
);

  wire not_1_out, not_2_out, not_3_out, not_4_out, not_5_out, not_6_out, not_7_out, or_1_out, or_2_out,
       or_3_out, or_4_out, or_5_out, or_6_out;

  not not_1 (not_1_out, b7);
  Multiplexer multiplexer_1 (.in0(b7), .in1(not_1_out), .out(Q7), .sel(or_1_out));
  or or_1 (or_1_out, or_2_out, Q6);
  not not_2 (not_2_out, b6);
  Multiplexer multiplexer_2 (.in0(b6), .in1(not_2_out), .out(Q6), .sel(or_2_out));
  or or_2 (or_2_out, or_3_out, Q5);
  Multiplexer multiplexer_3 (.in0(b5), .in1(not_3_out), .out(Q5), .sel(or_3_out));
  not not_3 (not_3_out, b5);
  or or_3 (or_3_out, or_4_out, Q4);
  not not_4 (not_4_out, b4);
  Multiplexer multiplexer_4 (.in0(b4), .in1(not_4_out), .out(Q4), .sel(or_4_out));
  or or_4 (or_4_out, or_5_out, Q3);
  not not_5 (not_5_out, b3);
  Multiplexer multiplexer_5 (.in0(b3), .in1(not_5_out), .out(Q3), .sel(or_5_out));
  or or_5 (or_5_out, or_6_out, Q2);
  not not_6 (not_6_out, b2);
  Multiplexer multiplexer_6 (.in0(b2), .in1(not_6_out), .out(Q2), .sel(or_6_out));
  or or_6 (or_6_out, b0, Q1);
  not not_7 (not_7_out, b1);
  Multiplexer multiplexer_7 (.in0(b1), .in1(not_7_out), .out(Q1), .sel(b0));

  assign Q0 = b0;
endmodule
