// Logisim project whole_circuit.circ as structural Verilog: 1 circuit, main circuit main
module main (
  input  [7:0] in_1,
  input  [7:0] in_2
);

  wire button_1_out, button_2_out, button_3_out, clock_1_out, control_unit_1_ea, control_unit_1_eb,
       control_unit_1_ep, control_unit_1_flg, control_unit_1_la, control_unit_1_lb, control_unit_1_psel,
       control_unit_1_sf, right_side_1_b0, right_side_1_b7, seg7_dec_1_a, seg7_dec_1_b, seg7_dec_1_c,
       seg7_dec_1_d, seg7_dec_1_e, seg7_dec_1_f, seg7_dec_1_g, seg7_dec_2_a, seg7_dec_2_b, seg7_dec_2_c,
       seg7_dec_2_d, seg7_dec_2_e, seg7_dec_2_f, seg7_dec_2_g, seg7_dec_3_a, seg7_dec_3_b, seg7_dec_3_c,
       seg7_dec_3_d, seg7_dec_3_e, seg7_dec_3_f, seg7_dec_3_g, sign_dec_1_a, sign_dec_1_b, sign_dec_1_c,
       sign_dec_1_d, sign_dec_1_e, sign_dec_1_f, sign_dec_1_g;
  wire [3:0] bcd_all_1_q1, bcd_all_1_q2, bcd_all_1_q3, dd_c_1_q0, dd_c_1_q1, dd_c_1_q2, dd_c_1_q3, dd_c_1_q4;
  wire [15:0] left_side_1_out_put;

  Button button_1 (.out(button_1_out));
  control_unit control_unit_1 (
    .Q7A(in_1[7]), .rst(button_1_out), .Q7B(right_side_1_b7), .CLK(clock_1_out), .B0(right_side_1_b0),
    .LA(control_unit_1_la), .LB(control_unit_1_lb), .SF(control_unit_1_sf), .flG(control_unit_1_flg),
    .psel(control_unit_1_psel), .EA(control_unit_1_ea), .EB(control_unit_1_eb), .EP(control_unit_1_ep));
  Clock clock_1 (.out(clock_1_out));
  Left_side left_side_1 (
    .A(in_1), .LA(control_unit_1_la), .EA(control_unit_1_ea), .EP(control_unit_1_ep),
    .b0(control_unit_1_psel), .Clk(clock_1_out), .rst(button_1_out), .out_put(left_side_1_out_put));
  right_side right_side_1 (
    .B(in_2), .EB(control_unit_1_eb), .LB(control_unit_1_lb), .clk(clock_1_out), .b0(right_side_1_b0),
    .b7(right_side_1_b7));  // open: z
  DD_C dd_c_1 (
    .Product(left_side_1_out_put[14:0]), .Q1(dd_c_1_q1), .Q0(dd_c_1_q0), .Q2(dd_c_1_q2), .Q4(dd_c_1_q4),
    .Q3(dd_c_1_q3));
  Button button_2 (.out(button_2_out));
  Button button_3 (.out(button_3_out));
  bcd_all bcd_all_1 (
    .flag(control_unit_1_flg), .D5(dd_c_1_q4), .D4(dd_c_1_q3), .D3(dd_c_1_q2), .D2(dd_c_1_q1),
    .D1(dd_c_1_q0), .sig_left(button_2_out), .sig_right(button_3_out), .CLK(clock_1_out), .Q1(bcd_all_1_q1),
    .Q2(bcd_all_1_q2), .Q3(bcd_all_1_q3));
  seg7_dec seg7_dec_1 (
    .x0(bcd_all_1_q1[0]), .x1(bcd_all_1_q1[1]), .x2(bcd_all_1_q1[2]), .x3(bcd_all_1_q1[3]), .a(seg7_dec_1_a),
    .b(seg7_dec_1_b), .c(seg7_dec_1_c), .d(seg7_dec_1_d), .e(seg7_dec_1_e), .f(seg7_dec_1_f), .g(seg7_dec_1_g));
  seg7_dec seg7_dec_2 (
    .x0(bcd_all_1_q2[0]), .x1(bcd_all_1_q2[1]), .x2(bcd_all_1_q2[2]), .x3(bcd_all_1_q2[3]), .a(seg7_dec_2_a),
    .b(seg7_dec_2_b), .c(seg7_dec_2_c), .d(seg7_dec_2_d), .e(seg7_dec_2_e), .f(seg7_dec_2_f), .g(seg7_dec_2_g));
  seg7_dec seg7_dec_3 (
    .x0(bcd_all_1_q3[0]), .x1(bcd_all_1_q3[1]), .x2(bcd_all_1_q3[2]), .x3(bcd_all_1_q3[3]), .a(seg7_dec_3_a),
    .b(seg7_dec_3_b), .c(seg7_dec_3_c), .d(seg7_dec_3_d), .e(seg7_dec_3_e), .f(seg7_dec_3_f), .g(seg7_dec_3_g));
  sign_dec sign_dec_1 (
    .SF(control_unit_1_sf), .a(sign_dec_1_a), .b(sign_dec_1_b), .c(sign_dec_1_c), .d(sign_dec_1_d),
    .e(sign_dec_1_e), .f(sign_dec_1_f), .g(sign_dec_1_g));
  _7_Segment_Display u_7_segment_display_1 (
    .g(seg7_dec_1_g), .f(seg7_dec_1_f), .a(seg7_dec_1_a), .b(seg7_dec_1_b), .e(seg7_dec_1_e),
    .d(seg7_dec_1_d), .c(seg7_dec_1_c));  // open: dp
  _7_Segment_Display u_7_segment_display_2 (
    .g(seg7_dec_2_g), .f(seg7_dec_2_f), .a(seg7_dec_2_a), .b(seg7_dec_2_b), .e(seg7_dec_2_e),
    .d(seg7_dec_2_d), .c(seg7_dec_2_c));  // open: dp
  _7_Segment_Display u_7_segment_display_3 (
    .g(seg7_dec_3_g), .f(seg7_dec_3_f), .a(seg7_dec_3_a), .b(seg7_dec_3_b), .e(seg7_dec_3_e),
    .d(seg7_dec_3_d), .c(seg7_dec_3_c));  // open: dp
  _7_Segment_Display u_7_segment_display_4 (
    .g(sign_dec_1_g), .f(sign_dec_1_f), .a(sign_dec_1_a), .b(sign_dec_1_b), .e(sign_dec_1_e),
    .d(sign_dec_1_d), .c(sign_dec_1_c));  // open: dp
endmodule
