// Logisim project twos_comp_circuit.circ as structural Verilog: 1 circuit, main circuit two_comp
module two_comp (
  input  B7,
  input  B6,
  input  B5,
  input  B4,
  input  B3,
  input  B2,
  input  B1,
  input  B0,
  output Q0,
  output Q1,
  output Q2,
  output Q3,
  output Q4,
  output Q5,
  output Q6,
  output Q7
);

  wire not_1_out, not_2_out, not_3_out, not_4_out, not_5_out, not_6_out, not_7_out, or_1_out, or_2_out,
       or_3_out, or_4_out, or_5_out, or_6_out;

  Multiplexer multiplexer_1 (.in0(B7), .in1(not_1_out), .out(Q7), .sel(or_1_out));
  or or_1 (or_1_out, or_2_out, B6);
  not not_1 (not_1_out, B7);
  not not_2 (not_2_out, B6);
  Multiplexer multiplexer_2 (.in0(B6), .in1(not_2_out), .out(Q6), .sel(or_2_out));
  or or_2 (or_2_out, or_3_out, B5);
  Multiplexer multiplexer_3 (.in0(B5), .in1(not_3_out), .out(Q5), .sel(or_3_out));
  or or_3 (or_3_out, or_4_out, B4);
  not not_3 (not_3_out, B5);
  not not_4 (not_4_out, B4);
  Multiplexer multiplexer_4 (.in0(B4), .in1(not_4_out), .out(Q4), .sel(or_4_out));
  or or_4 (or_4_out, or_5_out, B3);
  not not_5 (not_5_out, B3);
  Multiplexer multiplexer_5 (.in0(B3), .in1(not_5_out), .out(Q3), .sel(or_5_out));
  or or_5 (or_5_out, or_6_out, B2);
  not not_6 (not_6_out, B2);
  Multiplexer multiplexer_6 (.in0(B2), .in1(not_6_out), .out(Q2), .sel(or_6_out));
  or or_6 (or_6_out, B0, B1);
  Multiplexer multiplexer_7 (.in0(B1), .in1(not_7_out), .out(Q1), .sel(B0));
  not not_7 (not_7_out, B1);

  assign Q0 = B0;
endmodule
